// Logisim project Laboratorio_08.circ as structural Verilog: 6 circuits, main circuit Reg_Y
module Reg_Y (
  input  [3:0] Entrada,
  input  CLEAR,
  input  LOAD,
  input  CLOCK,
  output [3:0] \Saída 
);

  wire CLEAR_t, multiplexer_1_out, multiplexer_2_out, multiplexer_3_out, multiplexer_4_out;

  not not_1 (CLEAR_t, CLEAR);
  Multiplexer #(.disabled(0), .enable("false")) multiplexer_1 (
    .in0(\Saída [3]), .in1(Entrada[3]), .out(multiplexer_1_out), .sel(LOAD));
  D_Flip_Flop d_ff_1 (.clk(CLOCK), .D(multiplexer_1_out), .Q(\Saída [3]), .reset(CLEAR_t));  // open: Qn, preset, en
  Multiplexer #(.disabled(0), .enable("false")) multiplexer_2 (
    .in0(\Saída [2]), .in1(Entrada[2]), .out(multiplexer_2_out), .sel(LOAD));
  D_Flip_Flop d_ff_2 (.clk(CLOCK), .D(multiplexer_2_out), .Q(\Saída [2]), .reset(CLEAR_t));  // open: Qn, preset, en
  Multiplexer #(.disabled(0), .enable("false")) multiplexer_3 (
    .in0(\Saída [1]), .in1(Entrada[1]), .out(multiplexer_3_out), .sel(LOAD));
  D_Flip_Flop d_ff_3 (.clk(CLOCK), .D(multiplexer_3_out), .Q(\Saída [1]), .reset(CLEAR_t));  // open: Qn, preset, en
  Multiplexer #(.disabled(0), .enable("false")) multiplexer_4 (
    .in0(\Saída [0]), .in1(Entrada[0]), .out(multiplexer_4_out), .sel(LOAD));
  D_Flip_Flop d_ff_4 (.clk(CLOCK), .D(multiplexer_4_out), .Q(\Saída [0]), .reset(CLEAR_t));  // open: Qn, preset, en

  // Other names for the same wires on the sheet: E0 = Entrada[0]; E1 = Entrada[1]; E2 = Entrada[2]; E3 = Entrada[3];
  //   S0 = \Saída [0]; S1 = \Saída [1]; S2 = \Saída [2]; S3 = \Saída [3]
endmodule

module main (
  input  [3:0] Y_3_0,
  input  [3:0] C_11_0,
  input  LD_C,
  input  CLR_R,
  input  LD_R,
  input  CLOCK,
  input  EN_COD,
  input  [1:0] S_COD,
  input  LD_OUT,
  output [9:0] out_10
);

  wire adder_1_cout, C0, C1, C2;
  wire [3:0] Q0, Q1, Q2;
  wire [9:0] adder_1_out, adder_2_out, SOMA_0, SOMA_1, SOMA_2;

  Adder #(.width(10)) adder_1 (.a(SOMA_0), .b(SOMA_1), .out(adder_1_out), .cin(1'b0), .cout(adder_1_cout));
  Cod_2X4 cod_2x4_1 (.S_COD(S_COD), .EN_COD(EN_COD), .C0(C0), .C1(C1), .C2(C2));
  // Probe on Q0
  Reg_RxC reg_rxc_1 (
    .Y_3_0(Y_3_0), .C_3_0(C_11_0), .LD_C(C0), .CLR_R(CLR_R), .LD_R(LD_R), .CLOCK(CLOCK), .\Y_SAÍDA_3_0 (Q0),
    ._9_0(SOMA_0));
  // Probe on SOMA_0
  Adder #(.width(10)) adder_2 (.a(adder_1_out), .b(SOMA_2), .out(adder_2_out), .cin(adder_1_cout));  // open: cout
  // Probe on Q1
  Reg_RxC reg_rxc_2 (
    .Y_3_0(Q0), .C_3_0(C_11_0), .LD_C(C1), .CLR_R(CLR_R), .LD_R(LD_R), .CLOCK(CLOCK), .\Y_SAÍDA_3_0 (Q1),
    ._9_0(SOMA_1));
  // Probe on SOMA_1
  Reg reg_1 (.LOAD(LD_OUT), .CLOCK(CLOCK), .Entrada(adder_2_out), .\Saída (out_10));
  // Probe on Q2
  Reg_RxC reg_rxc_3 (
    .Y_3_0(Q1), .C_3_0(C_11_0), .LD_C(C2), .CLR_R(CLR_R), .LD_R(LD_R), .CLOCK(CLOCK), .\Y_SAÍDA_3_0 (Q2),
    ._9_0(SOMA_2));
  // Probe on SOMA_2

  // Other names for the same wires on the sheet: C[3:0] = C_11_0; CLEAR = CLR_R; LOAD_C = LD_C; LOAD_OUT = LD_OUT;
  //   LOAD_R = LD_R; SEL_C[1:0] = S_COD; Y[3:0] = Y_3_0
endmodule

module Reg_C (
  input  [3:0] Entrada,
  input  LOAD,
  input  CLOCK,
  output [3:0] \Saída 
);

  wire multiplexer_1_out, multiplexer_2_out, multiplexer_3_out, multiplexer_4_out;

  Multiplexer #(.disabled(0), .enable("false")) multiplexer_1 (
    .in0(\Saída [3]), .in1(Entrada[3]), .out(multiplexer_1_out), .sel(LOAD));
  D_Flip_Flop d_ff_1 (.clk(CLOCK), .D(multiplexer_1_out), .Q(\Saída [3]));  // open: Qn, preset, en, reset
  Multiplexer #(.disabled(0), .enable("false")) multiplexer_2 (
    .in0(\Saída [2]), .in1(Entrada[2]), .out(multiplexer_2_out), .sel(LOAD));
  D_Flip_Flop d_ff_2 (.clk(CLOCK), .D(multiplexer_2_out), .Q(\Saída [2]));  // open: Qn, preset, en, reset
  Multiplexer #(.disabled(0), .enable("false")) multiplexer_3 (
    .in0(\Saída [1]), .in1(Entrada[1]), .out(multiplexer_3_out), .sel(LOAD));
  D_Flip_Flop d_ff_3 (.clk(CLOCK), .D(multiplexer_3_out), .Q(\Saída [1]));  // open: Qn, preset, en, reset
  Multiplexer #(.disabled(0), .enable("false")) multiplexer_4 (
    .in0(\Saída [0]), .in1(Entrada[0]), .out(multiplexer_4_out), .sel(LOAD));
  D_Flip_Flop d_ff_4 (.clk(CLOCK), .D(multiplexer_4_out), .Q(\Saída [0]));  // open: Qn, preset, en, reset

  // Other names for the same wires on the sheet: E0 = Entrada[0]; E1 = Entrada[1]; E2 = Entrada[2]; E3 = Entrada[3];
  //   S0 = \Saída [0]; S1 = \Saída [1]; S2 = \Saída [2]; S3 = \Saída [3]
endmodule

module Reg_RxC (
  input  [3:0] Y_3_0,
  input  [3:0] C_3_0,
  input  LD_C,
  input  CLR_R,
  input  LD_R,
  input  CLOCK,
  output [3:0] \Y_SAÍDA_3_0 ,
  output [9:0] _9_0
);

  wire [3:0] \reg_c_1_saída ;

  // Probe on \Y_SAÍDA_3_0 
  Reg_Y reg_y_1 (.Entrada(Y_3_0), .CLEAR(CLR_R), .LOAD(LD_R), .CLOCK(CLOCK), .\Saída (\Y_SAÍDA_3_0 ));
  Reg_C reg_c_1 (.Entrada(C_3_0), .LOAD(LD_C), .CLOCK(CLOCK), .\Saída (\reg_c_1_saída ));
  // Probe on \reg_c_1_saída 
  Multiplier #(.width(4)) multiplier_1 (
    .a(\Y_SAÍDA_3_0 ), .b(\reg_c_1_saída ), .out(_9_0[3:0]), .cin(4'b0000), .cout(_9_0[7:4]));

  assign _9_0[9:8] = 2'b00;

  // Other names for the same wires on the sheet: C[3:0] = C_3_0; CLEAR = CLR_R; LOAD_C = LD_C; LOAD_R = LD_R;
  //   Y[3:0] = Y_3_0
endmodule

module Cod_2X4 (
  input  [1:0] S_COD,
  input  EN_COD,
  output C0,
  output C1,
  output C2
);

  Decoder #(.select(2), .disabled(0)) decoder_1 (
    .out0(C0), .out1(C1), .out2(C2), .sel(S_COD), .en(EN_COD));  // open: out3

  // Other names for the same wires on the sheet: LOAD_C = EN_COD; SEL_C[1:0] = S_COD
endmodule

module Reg (
  input  LOAD,
  input  CLOCK,
  input  [9:0] Entrada,
  output [9:0] \Saída 
);

  wire multiplexer_1_out, multiplexer_2_out, multiplexer_3_out, multiplexer_4_out, multiplexer_5_out,
       multiplexer_6_out, multiplexer_7_out, multiplexer_8_out, multiplexer_9_out, multiplexer_10_out;

  Multiplexer #(.disabled(0), .enable("false")) multiplexer_1 (
    .in0(\Saída [9]), .in1(Entrada[9]), .out(multiplexer_1_out), .sel(LOAD));
  Multiplexer #(.disabled(0), .enable("false")) multiplexer_2 (
    .in0(\Saída [8]), .in1(Entrada[8]), .out(multiplexer_2_out), .sel(LOAD));
  D_Flip_Flop d_ff_1 (.clk(CLOCK), .D(multiplexer_1_out), .Q(\Saída [9]));  // open: Qn, preset, en, reset
  D_Flip_Flop d_ff_2 (.clk(CLOCK), .D(multiplexer_2_out), .Q(\Saída [8]));  // open: Qn, preset, en, reset
  Multiplexer #(.disabled(0), .enable("false")) multiplexer_3 (
    .in0(\Saída [7]), .in1(Entrada[7]), .out(multiplexer_3_out), .sel(LOAD));
  D_Flip_Flop d_ff_3 (.clk(CLOCK), .D(multiplexer_3_out), .Q(\Saída [7]));  // open: Qn, preset, en, reset
  Multiplexer #(.disabled(0), .enable("false")) multiplexer_4 (
    .in0(\Saída [6]), .in1(Entrada[6]), .out(multiplexer_4_out), .sel(LOAD));
  D_Flip_Flop d_ff_4 (.clk(CLOCK), .D(multiplexer_4_out), .Q(\Saída [6]));  // open: Qn, preset, en, reset
  Multiplexer #(.disabled(0), .enable("false")) multiplexer_5 (
    .in0(\Saída [5]), .in1(Entrada[5]), .out(multiplexer_5_out), .sel(LOAD));
  D_Flip_Flop d_ff_5 (.clk(CLOCK), .D(multiplexer_5_out), .Q(\Saída [5]));  // open: Qn, preset, en, reset
  Multiplexer #(.disabled(0), .enable("false")) multiplexer_6 (
    .in0(\Saída [4]), .in1(Entrada[4]), .out(multiplexer_6_out), .sel(LOAD));
  D_Flip_Flop d_ff_6 (.clk(CLOCK), .D(multiplexer_6_out), .Q(\Saída [4]));  // open: Qn, preset, en, reset
  Multiplexer #(.disabled(0), .enable("false")) multiplexer_7 (
    .in0(\Saída [3]), .in1(Entrada[3]), .out(multiplexer_7_out), .sel(LOAD));
  D_Flip_Flop d_ff_7 (.clk(CLOCK), .D(multiplexer_7_out), .Q(\Saída [3]));  // open: Qn, preset, en, reset
  Multiplexer #(.disabled(0), .enable("false")) multiplexer_8 (
    .in0(\Saída [2]), .in1(Entrada[2]), .out(multiplexer_8_out), .sel(LOAD));
  D_Flip_Flop d_ff_8 (.clk(CLOCK), .D(multiplexer_8_out), .Q(\Saída [2]));  // open: Qn, preset, en, reset
  Multiplexer #(.disabled(0), .enable("false")) multiplexer_9 (
    .in0(\Saída [1]), .in1(Entrada[1]), .out(multiplexer_9_out), .sel(LOAD));
  D_Flip_Flop d_ff_9 (.clk(CLOCK), .D(multiplexer_9_out), .Q(\Saída [1]));  // open: Qn, preset, en, reset
  Multiplexer #(.disabled(0), .enable("false")) multiplexer_10 (
    .in0(\Saída [0]), .in1(Entrada[0]), .out(multiplexer_10_out), .sel(LOAD));
  D_Flip_Flop d_ff_10 (.clk(CLOCK), .D(multiplexer_10_out), .Q(\Saída [0]));  // open: Qn, preset, en, reset

  // Other names for the same wires on the sheet: E0 = Entrada[0]; E1 = Entrada[1]; E2 = Entrada[2]; E3 = Entrada[3];
  //   E4 = Entrada[4]; E5 = Entrada[5]; E6 = Entrada[6]; E7 = Entrada[7]; E8 = Entrada[8]; E9 = Entrada[9];
  //   S0 = \Saída [0]; S1 = \Saída [1]; S2 = \Saída [2]; S3 = \Saída [3]; S4 = \Saída [4]; S5 = \Saída [5];
  //   S6 = \Saída [6]; S7 = \Saída [7]; S8 = \Saída [8]; S9 = \Saída [9]
endmodule
